# Fritzing sketch console-2 (saved by Fritzing 0.9.3b)
breadboards: 1

parts:
  S1 = SWITCH-DPDT [package=ms]
  V1 = DC Power [voltage=12V]
  LM1 = RioRand LM2596
  Teensy1 = Teensy 3.0

nets:
  N1: S1.2, V1.V+
  N2: S1.3, LM1.Pin_0
  N3: V1.V-, LM1.Pin_1
  N4: LM1.Pin_2, Teensy1.Vin
  N5: LM1.Pin_3, Teensy1.GND
